# Fritzing sketch circuit (saved by Fritzing 0.9.3b)
breadboards: 1

parts:
  U1 = Sharp Dust Sensor [part_number=GP2Y1010AU0F]
  元件1 = Arduino Uno (Rev3)
  R1 = Resistor [tolerance=±5% resistance=150 package=THT]
  C1 = Electrolytic Capacitor [capacitance=0.22mF package="100 mil [THT, electrolytic]"]

nets:
  N1: U1.V-LED, R1.Pin_1, C1.+
  N2: U1.LED-GND, U1.S-GND, 元件1.GND, C1.-
  N3: U1.LED, 元件1.D2
  N4: U1.Vo, 元件1.A0
  VCC: U1.VCC, 元件1.5V, R1.Pin_0

custom parts:
  Sharp Dust Sensor: Sharp GP2Y1010AU0F Dust Sensor
